# Fritzing sketch ATtiny85 Fragrance Dispenser (saved by Fritzing 1.0.5)
circuit board: 5.09707cm x 4.02957cm
breadboards: 1

parts:
  R1 = PHOTOCELL [package=photocell-kit]
  R3 = Resistor [tolerance=±5% power=0.25W resistance=10k package=THT]
  U1 = ATTINY85 [package=dip]
  R2 = Resistor [tolerance=±5% power=0.25W resistance=220 mn=1 package=THT]
  S1 = Toggle Switch [package=THT]
  S2 = Toggle Switch [package=THT]
  LED1 = LED - 5mm [color="Red (633nm)" current=0.030A package="5 mm [THT]"]
  M3 = Dagu DGServo 9g (Top view) [part_number=RS001B]
  VCC1 = Battery [internal_resistance=0.1Ω]
  IC1 = Switching step-up voltage regulator [package=sot23-5]

nets:
  N1: R1.P$1, R3.Pin_1, U1.PB3(ADC3)
  VCC: R1.P$2, U1.VCC, M3.vcc, IC1.OUT
  GND: R3.Pin_0, U1.GND, S1.COM, S2.COM, LED1.cathode, M3.gnd, VCC1.-, IC1.GND
  N2: U1.PB4(ADC2), R2.Pin_1
  N3: U1.PB0(MOSI), M3.pulse
  N4: U1.PB1(MISO), S1.L2
  N5: U1.PB2(SCK_ADC1), S2.L2
  N6: R2.Pin_0, LED1.anode
  N7: VCC1.+, IC1.EN

custom parts:
  ATTINY85: Atmel 8-pin 2/4/8kB flash uC
